# Fritzing sketch IO Bus (saved by Fritzing 0.8.7b)
breadboards: 1

parts:
  INPUT-J1 = male pin header, 6 pins [form="♂ (male)"]
  INPUT-J2 = male pin header, 6 pins [form="♂ (male)"]
  OUTPUT-J3 = male pin header, 6 pins [form="♂ (male)"]
  OUTPUT-J4 = male pin header, 6 pins [form="♂ (male)"]
  74LS138 = 74LS138 [part_number=74LS138 package="DIP (Dual Inline) [THT]"]
  J5 = male pin header, 10 pins [form="♂ (male)"]
  R1 = Resistor [tolerance=±5% resistance=10k package=THT]

nets:
  N1: INPUT-J1.pin1, INPUT-J2.pin1, OUTPUT-J3.pin1, OUTPUT-J4.pin1, 74LS138.~E3, 74LS138.VCC, J5.pin5, R1.Pin_1
  N2: INPUT-J1.pin2, INPUT-J2.pin2, OUTPUT-J3.pin2, OUTPUT-J4.pin2, 74LS138.~E2, 74LS138.GND, J5.pin6
  N3: INPUT-J1.pin3, INPUT-J2.pin3, J5.pin7
  N4: INPUT-J1.pin4, 74LS138.~O0
  N5: INPUT-J1.pin5, INPUT-J2.pin5, OUTPUT-J3.pin5, OUTPUT-J4.pin5, J5.pin9
  N6: INPUT-J1.pin6, INPUT-J2.pin6, OUTPUT-J3.pin6, OUTPUT-J4.pin6, J5.pin10
  N7: INPUT-J2.pin4, 74LS138.~O1
  N8: OUTPUT-J3.pin3, OUTPUT-J4.pin3, J5.pin8
  N9: OUTPUT-J3.pin4, 74LS138.~O4
  N10: OUTPUT-J4.pin4, 74LS138.~O5
  N11: 74LS138.A, J5.pin1
  N12: 74LS138.B, J5.pin2
  N13: 74LS138.C, J5.pin3
  N14: 74LS138.~E1, J5.pin4, R1.Pin_0

notes:
  A0
  A1
  A2
  EN
  VCC
  GND
  MISO
  MOSI
  CLK
  LOAD

custom parts:
  74LS138: High speed 1-of-8 Decoder/ Demultiplexer
